# Fritzing sketch tea_timer (saved by Fritzing 0.9.2b)

parts:
  LCD = LCD screen
  ARDUINO_PRO_MINI = Arduino Pro Mini v13
  POW_JACK = Power Jack [package=power_jack_pth]
  CONT_POT = Rotary Potentiometer (Small) [package=THT]
  SEL_POT = Rotary Potentiometer (Small) [package=THT]
  SEL_SW = Pushbutton [package="[SMD]"]
  POW_SW = Toggle Switch [package=THT]
  SERVO = Basic Servo
  BUZZER = Piezo Speaker

nets:
  GND: LCD.VSS, LCD.R/W, LCD.LED-, ARDUINO_PRO_MINI.GND, POW_JACK.GND, CONT_POT.leg1, SEL_POT.leg1, SEL_SW.Pin_1, SEL_SW.Pin_2, SERVO.gnd, BUZZER.pin1
  VCC: LCD.VDD, ARDUINO_PRO_MINI.VCC, CONT_POT.leg2, SEL_POT.leg2, POW_SW.L2, SERVO.vcc
  N1: LCD.V0, CONT_POT.wiper
  N2: LCD.RS, ARDUINO_PRO_MINI.D12/MISO
  N3: LCD.E, ARDUINO_PRO_MINI.D11_PWM/MOSI
  N4: LCD.DB4, ARDUINO_PRO_MINI.D6_PWM
  N5: LCD.DB5, ARDUINO_PRO_MINI.D5_PWM
  N6: LCD.DB6, ARDUINO_PRO_MINI.D4
  N7: LCD.DB7, ARDUINO_PRO_MINI.D3_PWM
  N8: LCD.LED+, ARDUINO_PRO_MINI.D9_PWM
  N9: ARDUINO_PRO_MINI.A0, SEL_POT.wiper
  N10: ARDUINO_PRO_MINI.D8, BUZZER.pin2
  N11: ARDUINO_PRO_MINI.D7, SERVO.pulse
  N12: ARDUINO_PRO_MINI.D2, SEL_SW.Pin_3, SEL_SW.Pin_4
  N13: POW_JACK.PWR, POW_SW.COM

custom parts:
  Rotary Potentiometer (Small): A rotary adjustable resistor (potentiometer).
